# Fritzing sketch arduino-powerctl-schematics (saved by Fritzing 0.9.9b)
breadboards: 2

parts:
  DS2Y-5-DC5V1 = DS2Y-5-DC5V [part_number=DS2Y-5-DC5V]
  Part1 = Arduino Nano (Rev3.0)
  LED1 = LED - 3mm [color="Green (555nm)" current=0.030 package="3 mm [THT]"]
  LED2 = LED - 3mm [color="Red (633nm)" current=0.030 package="3 mm [THT]"]
  LED3 = LED - 3mm [color="Green (555nm)" current=0.030 package="3 mm [THT]"]
  R1 = Resistor [tolerance=±5% resistance=680 package="2512 [SMD]"]
  R2 = Resistor [tolerance=±5% resistance=680 package="2512 [SMD]"]
  R3 = Resistor [tolerance=±5% resistance=680 package="2512 [SMD]"]
  S2 = Pushbutton [package="[THT]"]
  S3 = Pushbutton [package="[THT]"]
  Q1 = NPN-Transistor [package="TO92 [THT]"]
  D1 = Diode [package=diode-hv]
  R4 = Resistor [tolerance=±5% resistance=10k package="2512 [SMD]"]
  R5 = Temperature Sensor (Thermistor) [thermistor_type=NTC package=THT]
  R6 = Resistor [tolerance=±5% resistance=10k package="2512 [SMD]"]
  Q2 = NPN-Transistor [package="TO92 [THT]"]
  R7 = Resistor [tolerance=±5% resistance=330 package="2512 [SMD]"]
  F1 = Fan - Ventilador [package=THT]
  C1 = Capacitor Polarized [package=panasonic_d]
  D2 = Rectifier Diode 10A [part_number=P1000K]
  Mod1 = Raspberry Pi 4B
  R8 = Resistor [tolerance=±5% resistance=2.2k package="2512 [SMD]"]
  R9 = Resistor [tolerance=±5% resistance=3.3k package="2512 [SMD]"]

nets:
  VIN: DS2Y-5-DC5V1.4_COM, DS2Y-5-DC5V1.1_+, Part1.VIN, D1.C, F1.5V, C1.+, D2.cathode
  N1: DS2Y-5-DC5V1.16_-, Q1.C
  N2: Part1.D1/TX, R8.Pin_1
  N3: Part1.D0/RX, Mod1.GPIO14
  GND: Part1.GND, LED1.cathode, LED2.cathode, LED3.cathode, S2.Pin_3, S2.Pin_4, Q1.E, R5.pin_0, Q2.E, Mod1.GND, R9.Pin_0
  N4: Part1.D2, R4.Pin_1
  N5: Part1.D5, R7.Pin_1
  N6: Part1.D8, S2.Pin_1, S2.Pin_2
  N7: Part1.D9, R2.Pin_1
  N8: Part1.D10, R3.Pin_1
  N9: Part1.D11/MOSI, R1.Pin_1
  N10: Part1.A0, R5.pin_1, R6.Pin_0
  N11: Part1.AREF, Part1.3V3, R6.Pin_1
  N12: LED1.anode, R3.Pin_0
  N13: LED2.anode, R1.Pin_0
  N14: LED3.anode, R2.Pin_0
  N15: S3.Pin_1, S3.Pin_2
  N16: S3.Pin_3, S3.Pin_4
  N17: Q1.B, R4.Pin_0
  N18: Q2.B, R7.Pin_0
  N19: Q2.C, F1.GND, C1.-, D2.anode
  N20: Mod1.GPIO15, R8.Pin_0, R9.Pin_1

notes:
  main 5V power

custom parts:
  Fan - Ventilador: Ventilador de 2 pines, se encuentra comunmente en computadoras de escritorio
